// Digital circuit day23.dig as structural Verilog
module day23 (
  input  C,
  output [31:0] cycles,
  output [63:0] Y
);

  wire and_1_out, and_3_out, C_t, comparator_1_gt, comparator_2_lt, comparator_3_eq, comparator_4_eq,
       comparator_5_eq, day23_parser_1_nextout_en, day23_parser_1_out_en, day23_parser_1_out_y,
       demultiplexer_1_out_0, demultiplexer_1_out_1, node0_p3, node0_p4, node0_p5, node0_p7, node0_p9,
       node0_p10, node1_p3, node1_p5, node1_p7, node1_p9, node1_p10, node2_p3, node2_p5, node2_p7, node2_p9,
       node2_p10, node3_p3, node3_p5, node3_p7, node3_p9, node3_p10, node4_p3, node4_p5, node4_p7, node4_p9,
       node4_p10, node5_p3, node5_p5, node5_p7, node5_p9, node5_p10, node6_p3, node6_p5, node6_p7, node6_p9,
       node6_p10, node7_p3, node7_p5, node7_p7, node7_p9, node7_p10, node8_p3, node8_p5, node8_p7, node8_p9,
       node8_p10, node9_p3, node9_p5, node9_p7, node9_p9, node9_p10, node10_p3, node10_p5, node10_p7,
       node10_p9, node10_p10, node11_p3, node11_p5, node11_p7, node11_p9, node11_p10, node12_p3, node12_p5,
       node12_p7, node12_p9, node12_p10, node13_p3, node13_p5, node13_p7, node13_p9, node13_p10, node14_p3,
       node14_p5, node14_p7, node14_p9, node14_p10, node15_p3, node15_p5, node15_p7, node15_p9, node15_p10,
       node16_p3, node16_p5, node16_p7, node16_p9, node16_p10, node17_p3, node17_p5, node17_p7, node17_p9,
       node17_p10, node18_p3, node18_p5, node18_p7, node18_p9, node18_p10, node19_p3, node19_p5, node19_p7,
       node19_p9, node19_p10, node20_p3, node20_p5, node20_p7, node20_p9, node20_p10, node21_p3, node21_p5,
       node21_p7, node21_p9, node21_p10, node22_p3, node22_p5, node22_p7, node22_p9, node22_p10, node23_p3,
       node23_p5, node23_p7, node23_p9, node23_p10, node24_p3, node24_p5, node24_p7, node24_p9, node24_p10,
       node25_p3, node25_p5, node25_p7, node25_p9, node25_p10, node26_p3, node26_p5, node26_p7, node26_p9,
       node26_p10, node27_p3, node27_p5, node27_p7, node27_p9, node27_p10, node28_p3, node28_p5, node28_p7,
       node28_p9, node28_p10, node29_p3, node29_p5, node29_p7, node29_p9, node29_p10, node30_p3, node30_p5,
       node30_p7, node30_p9, node30_p10, node31_p3, node31_p5, node31_p7, node31_p9, node31_p10, node32_p3,
       node32_p5, node32_p7, node32_p9, node32_p10, node33_p3, node33_p5, node33_p7, node33_p9, node33_p10,
       node34_p3, node34_p5, node34_p7, node34_p9, node34_p10, node35_p3, node35_p5, node35_p7, node35_p9,
       node35_p10, node36_p3, node36_p5, node36_p7, node36_p9, node36_p10, node37_p3, node37_p5, node37_p7,
       node37_p9, node37_p10, node38_p3, node38_p5, node38_p7, node38_p9, node38_p10, node39_p3, node39_p5,
       node39_p7, node39_p9, node39_p10, node40_p3, node40_p5, node40_p7, node40_p9, node40_p10, node41_p3,
       node41_p5, node41_p7, node41_p9, node41_p10, node42_p3, node42_p5, node42_p7, node42_p9, node42_p10,
       node43_p3, node43_p5, node43_p7, node43_p9, node43_p10, node44_p3, node44_p5, node44_p7, node44_p9,
       node44_p10, node45_p3, node45_p5, node45_p7, node45_p9, node45_p10, node46_p3, node46_p5, node46_p7,
       node46_p9, node46_p10, node47_p3, node47_p5, node47_p7, node47_p9, node47_p10, node48_p3, node48_p5,
       node48_p7, node48_p9, node48_p10, node49_p4, node49_p8, node49_p9, not_1_out, or_1_out, shifter_1_p5,
       shifter_1_p8, shifter_1_p9, shifter_1_p10, shifter_1_p11;
  wire [3:0] div_1_r, div_2_r, div_3_r, div_4_r, div_5_r, phase_out;
  wire [63:0] day23_parser_1_nextout_val, day23_parser_1_out_val, div_2_q, div_3_q, div_4_q, div_5_q,
       node0_p6, node49_p6, shifter_1_p2, shifter_1_p6, shifter_1_p7, X_q, Y_q;
  wire [63:4] div_1_r_2, div_2_r_2, div_3_r_2, div_4_r_2, div_5_r_2;

  // day23_node #(.generic("label := \"node0\";")) node0: pin names not known; wires that end beside it: C_t, {64{1'b0}}, node0_p3, node0_p4, node0_p5, node0_p6, node0_p7, 1'b0, node0_p9, node0_p10
  // day23_node #(.generic("label := \"node1\";")) node1: pin names not known; wires that end beside it: C_t, node0_p3, node1_p3, node0_p5, node1_p5, node0_p7, node1_p7, node0_p9, node1_p9, node1_p10
  // day23_node #(.generic("label := \"node2\";")) node2: pin names not known; wires that end beside it: C_t, node1_p3, node2_p3, node1_p5, node2_p5, node1_p7, node2_p7, node1_p9, node2_p9, node2_p10
  // day23_node #(.generic("label := \"node3\";")) node3: pin names not known; wires that end beside it: C_t, node2_p3, node3_p3, node2_p5, node3_p5, node2_p7, node3_p7, node2_p9, node3_p9, node3_p10
  // day23_node #(.generic("label := \"node4\";")) node4: pin names not known; wires that end beside it: C_t, node3_p3, node4_p3, node3_p5, node4_p5, node3_p7, node4_p7, node3_p9, node4_p9, node4_p10
  // day23_node #(.generic("label := \"node5\";")) node5: pin names not known; wires that end beside it: C_t, node4_p3, node5_p3, node4_p5, node5_p5, node4_p7, node5_p7, node4_p9, node5_p9, node5_p10
  // day23_node #(.generic("label := \"node6\";")) node6: pin names not known; wires that end beside it: C_t, node5_p3, node6_p3, node5_p5, node6_p5, node5_p7, node6_p7, node5_p9, node6_p9, node6_p10
  // day23_node #(.generic("label := \"node7\";")) node7: pin names not known; wires that end beside it: C_t, node6_p3, node7_p3, node6_p5, node7_p5, node6_p7, node7_p7, node6_p9, node7_p9, node7_p10
  // day23_node #(.generic("label := \"node8\";")) node8: pin names not known; wires that end beside it: C_t, node7_p3, node8_p3, node7_p5, node8_p5, node7_p7, node8_p7, node7_p9, node8_p9, node8_p10
  // day23_node #(.generic("label := \"node9\";")) node9: pin names not known; wires that end beside it: C_t, node8_p3, node9_p3, node8_p5, node9_p5, node8_p7, node9_p7, node8_p9, node9_p9, node9_p10
  // day23_node #(.generic("label := \"node10\";")) node10: pin names not known; wires that end beside it: C_t, node9_p3, node10_p3, node9_p5, node10_p5, node9_p7, node10_p7, node9_p9, node10_p9, node10_p10
  // day23_node #(.generic("label := \"node11\";")) node11: pin names not known; wires that end beside it: C_t, node10_p3, node11_p3, node10_p5, node11_p5, node10_p7, node11_p7, node10_p9, node11_p9, node11_p10
  // day23_node #(.generic("label := \"node12\";")) node12: pin names not known; wires that end beside it: C_t, node11_p3, node12_p3, node11_p5, node12_p5, node11_p7, node12_p7, node11_p9, node12_p9, node12_p10
  // day23_node #(.generic("label := \"node13\";")) node13: pin names not known; wires that end beside it: C_t, node12_p3, node13_p3, node12_p5, node13_p5, node12_p7, node13_p7, node12_p9, node13_p9, node13_p10
  // day23_node #(.generic("label := \"node14\";")) node14: pin names not known; wires that end beside it: C_t, node13_p3, node14_p3, node13_p5, node14_p5, node13_p7, node14_p7, node13_p9, node14_p9, node14_p10
  // day23_node #(.generic("label := \"node15\";")) node15: pin names not known; wires that end beside it: C_t, node14_p3, node15_p3, node14_p5, node15_p5, node14_p7, node15_p7, node14_p9, node15_p9, node15_p10
  LED led_1 (.in(node0_p10));
  LED led_2 (.in(node1_p10));
  LED led_3 (.in(node2_p10));
  LED led_4 (.in(node3_p10));
  LED led_5 (.in(node4_p10));
  LED led_6 (.in(node5_p10));
  LED led_7 (.in(node6_p10));
  LED led_8 (.in(node7_p10));
  LED led_9 (.in(node8_p10));
  LED led_10 (.in(node9_p10));
  LED led_11 (.in(node10_p10));
  LED led_12 (.in(node11_p10));
  LED led_13 (.in(node12_p10));
  LED led_14 (.in(node13_p10));
  LED led_15 (.in(node14_p10));
  LED led_16 (.in(node15_p10));
  // day23_node #(.generic("label := \"node16\";")) node16: pin names not known; wires that end beside it: C_t, node15_p3, node16_p3, node15_p5, node16_p5, node15_p7, node16_p7, node15_p9, node16_p9, node16_p10
  // day23_node #(.generic("label := \"node17\";")) node17: pin names not known; wires that end beside it: C_t, node16_p3, node17_p3, node16_p5, node17_p5, node16_p7, node17_p7, node16_p9, node17_p9, node17_p10
  // day23_node #(.generic("label := \"node18\";")) node18: pin names not known; wires that end beside it: C_t, node17_p3, node18_p3, node17_p5, node18_p5, node17_p7, node18_p7, node17_p9, node18_p9, node18_p10
  // day23_node #(.generic("label := \"node19\";")) node19: pin names not known; wires that end beside it: C_t, node18_p3, node19_p3, node18_p5, node19_p5, node18_p7, node19_p7, node18_p9, node19_p9, node19_p10
  // day23_node #(.generic("label := \"node20\";")) node20: pin names not known; wires that end beside it: C_t, node19_p3, node20_p3, node19_p5, node20_p5, node19_p7, node20_p7, node19_p9, node20_p9, node20_p10
  // day23_node #(.generic("label := \"node21\";")) node21: pin names not known; wires that end beside it: C_t, node20_p3, node21_p3, node20_p5, node21_p5, node20_p7, node21_p7, node20_p9, node21_p9, node21_p10
  // day23_node #(.generic("label := \"node22\";")) node22: pin names not known; wires that end beside it: C_t, node21_p3, node22_p3, node21_p5, node22_p5, node21_p7, node22_p7, node21_p9, node22_p9, node22_p10
  // day23_node #(.generic("label := \"node23\";")) node23: pin names not known; wires that end beside it: C_t, node22_p3, node23_p3, node22_p5, node23_p5, node22_p7, node23_p7, node22_p9, node23_p9, node23_p10
  // day23_node #(.generic("label := \"node24\";")) node24: pin names not known; wires that end beside it: C_t, node23_p3, node24_p3, node23_p5, node24_p5, node23_p7, node24_p7, node23_p9, node24_p9, node24_p10
  // day23_node #(.generic("label := \"node25\";")) node25: pin names not known; wires that end beside it: C_t, node24_p3, node25_p3, node24_p5, node25_p5, node24_p7, node25_p7, node24_p9, node25_p9, node25_p10
  // day23_node #(.generic("label := \"node26\";")) node26: pin names not known; wires that end beside it: C_t, node25_p3, node26_p3, node25_p5, node26_p5, node25_p7, node26_p7, node25_p9, node26_p9, node26_p10
  // day23_node #(.generic("label := \"node27\";")) node27: pin names not known; wires that end beside it: C_t, node26_p3, node27_p3, node26_p5, node27_p5, node26_p7, node27_p7, node26_p9, node27_p9, node27_p10
  // day23_node #(.generic("label := \"node28\";")) node28: pin names not known; wires that end beside it: C_t, node27_p3, node28_p3, node27_p5, node28_p5, node27_p7, node28_p7, node27_p9, node28_p9, node28_p10
  // day23_node #(.generic("label := \"node29\";")) node29: pin names not known; wires that end beside it: C_t, node28_p3, node29_p3, node28_p5, node29_p5, node28_p7, node29_p7, node28_p9, node29_p9, node29_p10
  // day23_node #(.generic("label := \"node30\";")) node30: pin names not known; wires that end beside it: C_t, node29_p3, node30_p3, node29_p5, node30_p5, node29_p7, node30_p7, node29_p9, node30_p9, node30_p10
  // day23_node #(.generic("label := \"node31\";")) node31: pin names not known; wires that end beside it: C_t, node30_p3, node31_p3, node30_p5, node31_p5, node30_p7, node31_p7, node30_p9, node31_p9, node31_p10
  LED led_17 (.in(node16_p10));
  LED led_18 (.in(node17_p10));
  LED led_19 (.in(node18_p10));
  LED led_20 (.in(node19_p10));
  LED led_21 (.in(node20_p10));
  LED led_22 (.in(node21_p10));
  LED led_23 (.in(node22_p10));
  LED led_24 (.in(node23_p10));
  LED led_25 (.in(node24_p10));
  LED led_26 (.in(node25_p10));
  LED led_27 (.in(node26_p10));
  LED led_28 (.in(node27_p10));
  LED led_29 (.in(node28_p10));
  LED led_30 (.in(node29_p10));
  LED led_31 (.in(node30_p10));
  LED led_32 (.in(node31_p10));
  // day23_node #(.generic("label := \"node32\";")) node32: pin names not known; wires that end beside it: C_t, node31_p3, node32_p3, node31_p5, node32_p5, node31_p7, node32_p7, node31_p9, node32_p9, node32_p10
  // day23_node #(.generic("label := \"node33\";")) node33: pin names not known; wires that end beside it: C_t, node32_p3, node33_p3, node32_p5, node33_p5, node32_p7, node33_p7, node32_p9, node33_p9, node33_p10
  // day23_node #(.generic("label := \"node34\";")) node34: pin names not known; wires that end beside it: C_t, node33_p3, node34_p3, node33_p5, node34_p5, node33_p7, node34_p7, node33_p9, node34_p9, node34_p10
  // day23_node #(.generic("label := \"node35\";")) node35: pin names not known; wires that end beside it: C_t, node34_p3, node35_p3, node34_p5, node35_p5, node34_p7, node35_p7, node34_p9, node35_p9, node35_p10
  // day23_node #(.generic("label := \"node36\";")) node36: pin names not known; wires that end beside it: C_t, node35_p3, node36_p3, node35_p5, node36_p5, node35_p7, node36_p7, node35_p9, node36_p9, node36_p10
  // day23_node #(.generic("label := \"node37\";")) node37: pin names not known; wires that end beside it: C_t, node36_p3, node37_p3, node36_p5, node37_p5, node36_p7, node37_p7, node36_p9, node37_p9, node37_p10
  // day23_node #(.generic("label := \"node38\";")) node38: pin names not known; wires that end beside it: C_t, node37_p3, node38_p3, node37_p5, node38_p5, node37_p7, node38_p7, node37_p9, node38_p9, node38_p10
  // day23_node #(.generic("label := \"node39\";")) node39: pin names not known; wires that end beside it: C_t, node38_p3, node39_p3, node38_p5, node39_p5, node38_p7, node39_p7, node38_p9, node39_p9, node39_p10
  // day23_node #(.generic("label := \"node40\";")) node40: pin names not known; wires that end beside it: C_t, node39_p3, node40_p3, node39_p5, node40_p5, node39_p7, node40_p7, node39_p9, node40_p9, node40_p10
  // day23_node #(.generic("label := \"node41\";")) node41: pin names not known; wires that end beside it: C_t, node40_p3, node41_p3, node40_p5, node41_p5, node40_p7, node41_p7, node40_p9, node41_p9, node41_p10
  // day23_node #(.generic("label := \"node42\";")) node42: pin names not known; wires that end beside it: C_t, node41_p3, node42_p3, node41_p5, node42_p5, node41_p7, node42_p7, node41_p9, node42_p9, node42_p10
  // day23_node #(.generic("label := \"node43\";")) node43: pin names not known; wires that end beside it: C_t, node42_p3, node43_p3, node42_p5, node43_p5, node42_p7, node43_p7, node42_p9, node43_p9, node43_p10
  // day23_node #(.generic("label := \"node44\";")) node44: pin names not known; wires that end beside it: C_t, node43_p3, node44_p3, node43_p5, node44_p5, node43_p7, node44_p7, node43_p9, node44_p9, node44_p10
  // day23_node #(.generic("label := \"node45\";")) node45: pin names not known; wires that end beside it: C_t, node44_p3, node45_p3, node44_p5, node45_p5, node44_p7, node45_p7, node44_p9, node45_p9, node45_p10
  // day23_node #(.generic("label := \"node46\";")) node46: pin names not known; wires that end beside it: C_t, node45_p3, node46_p3, node45_p5, node46_p5, node45_p7, node46_p7, node45_p9, node46_p9, node46_p10
  // day23_node #(.generic("label := \"node47\";")) node47: pin names not known; wires that end beside it: C_t, node46_p3, node47_p3, node46_p5, node47_p5, node46_p7, node47_p7, node46_p9, node47_p9, node47_p10
  LED led_33 (.in(node32_p10));
  LED led_34 (.in(node33_p10));
  LED led_35 (.in(node34_p10));
  LED led_36 (.in(node35_p10));
  LED led_37 (.in(node36_p10));
  LED led_38 (.in(node37_p10));
  LED led_39 (.in(node38_p10));
  LED led_40 (.in(node39_p10));
  LED led_41 (.in(node40_p10));
  LED led_42 (.in(node41_p10));
  LED led_43 (.in(node42_p10));
  LED led_44 (.in(node43_p10));
  LED led_45 (.in(node44_p10));
  LED led_46 (.in(node45_p10));
  LED led_47 (.in(node46_p10));
  LED led_48 (.in(node47_p10));
  // day23_node #(.generic("label := \"node48\";")) node48: pin names not known; wires that end beside it: C_t, node47_p3, node48_p3, node47_p5, node48_p5, node47_p7, node48_p7, node47_p9, node48_p9, node48_p10
  // day23_node #(.generic("label := \"node49\";")) node49: pin names not known; wires that end beside it: C_t, node48_p3, node48_p5, node49_p4, node48_p7, node49_p6, node48_p9, node49_p8, node49_p9
  Seven_Seg_Hex seven_seg_hex_1 (.d(div_1_r), .dp(1'b0));
  Div #(.Bits(64)) div_1 (.a(div_2_q), .b(64'ha), .r({div_1_r_2, div_1_r}));  // open: q
  Seven_Seg_Hex seven_seg_hex_2 (.d(div_2_r), .dp(1'b0));
  Div #(.Bits(64)) div_2 (.a(div_3_q), .b(64'ha), .q(div_2_q), .r({div_2_r_2, div_2_r}));
  not not_1 (not_1_out, node49_p8);
  day23_parser day23_parser_1 (
    .in_en(node49_p4), .in_val(node49_p6), .address(64'hff), .C(C_t), .out_en(day23_parser_1_out_en),
    .out_val(day23_parser_1_out_val), .nextout_en(day23_parser_1_nextout_en),
    .nextout_val(day23_parser_1_nextout_val), .out_y(day23_parser_1_out_y));
  Seven_Seg_Hex seven_seg_hex_3 (.d(div_3_r), .dp(1'b0));
  LED led_49 (.in(node48_p10));
  LED led_50 (.in(node49_p9));
  Div #(.Bits(64)) div_3 (.a(div_4_q), .b(64'ha), .q(div_3_q), .r({div_3_r_2, div_3_r}));
  Seven_Seg_Hex seven_seg_hex_4 (.d(div_4_r), .dp(1'b0));
  Div #(.Bits(64)) div_4 (.a(div_5_q), .b(64'ha), .q(div_4_q), .r({div_4_r_2, div_4_r}));
  Seven_Seg_Hex seven_seg_hex_5 (.d(div_5_r), .dp(and_3_out));
  Div #(.Bits(64)) div_5 (.a(Y), .b(64'ha), .q(div_5_q), .r({div_5_r_2, div_5_r}));
  Comparator #(.Bits(4)) comparator_1 (.a(phase_out), .b(4'b0000), .gt(comparator_1_gt));  // open: eq, lt
  Comparator #(.Bits(4)) comparator_2 (.a(phase_out), .b(4'b0011), .lt(comparator_2_lt));  // open: gt, eq
  Demultiplexer demultiplexer_1 (
    .sel(day23_parser_1_out_y), .in(day23_parser_1_out_en), .out_0(demultiplexer_1_out_0),
    .out_1(demultiplexer_1_out_1));
  or or_1 (or_1_out, not_1_out, comparator_1_gt);
  Register #(.Bits(64)) X (.D(day23_parser_1_out_val), .C(C_t), .en(demultiplexer_1_out_0), .Q(X_q));
  and and_1 (and_1_out, or_1_out, comparator_2_lt);
  // shifter shifter_1: pin names not known; wires that end beside it: and_1_out, shifter_1_p2, C_t, Y, shifter_1_p5, shifter_1_p6, shifter_1_p7, shifter_1_p8, shifter_1_p9, shifter_1_p10, shifter_1_p11
  // Probe on X_q
  Counter #(.Bits(4)) phase (.en(or_1_out), .C(C_t), .clr(1'b0), .out(phase_out));  // open: ovf
  Counter #(.Bits(32)) u_cycles (.en(1'b1), .C(C_t), .clr(1'b0), .out(cycles));  // open: ovf
  Register #(.Bits(64)) u_Y (.D(day23_parser_1_out_val), .C(C_t), .en(demultiplexer_1_out_1), .Q(Y_q));
  Multiplexer #(.Selector_Bits(2), .Bits(64)) multiplexer_1 (
    .sel(phase_out[1:0]), .in_0({64{1'b0}}), .in_1(X_q), .in_2(Y_q), .in_3({64{1'b0}}), .out(shifter_1_p2));
  day23_merger day23_merger_1 (
    .C(C_t), .in1_en(and_1_out), .in1_val(shifter_1_p2), .in2_en(day23_parser_1_nextout_en),
    .in2_val(day23_parser_1_nextout_val), .out_en(node0_p4), .out_val(node0_p6));
  Comparator #(.Bits(64)) comparator_3 (.a(shifter_1_p6), .b({64{1'b0}}), .eq(comparator_3_eq));  // open: gt, lt
  // Probe on Y_q
  Comparator #(.Bits(64)) comparator_4 (.a(shifter_1_p7), .b(Y), .eq(comparator_4_eq));  // open: gt, lt
  and and_2 (C_t, ~and_3_out, C);  // And
  and and_3 (and_3_out, ~comparator_5_eq, comparator_4_eq, comparator_3_eq);  // And
  Break #(.Cycles(420000)) stable (.brk(and_3_out));
  // Probe on Y
  // Probe on shifter_1_p5
  // Probe on shifter_1_p6
  // Probe on shifter_1_p7
  // Probe on shifter_1_p8
  // Probe on shifter_1_p9
  // Probe on shifter_1_p10
  // Probe on shifter_1_p11
  Comparator #(.Bits(64)) comparator_5 (.a(shifter_1_p7), .b({64{1'b0}}), .eq(comparator_5_eq));  // open: gt, lt

  // Notes on the sheet:
  //   C: Hz: 4000
endmodule
