// Digital circuit intcode.dig as structural Verilog
module intcode (
  input  clock,
  input  [63:0] in_val,
  input  in_avail,
  output [63:0] write_val,
  output [15:0] rw_addr,
  output write_en,
  output [15:0] pc,
  output [63:0] X,
  output [63:0] Y,
  output [63:0] r,
  output [63:0] instr,
  output [1:0] phase,
  output out_en,
  output [63:0] out_val,
  output [31:0] cycle_cnt,
  output running,
  output in_req
);

  wire advance, and_2_out, and_3_out, and_4_out, and_5_out, and_6_out, and_7_out, and_8_out, and_9_out, C,
       C_t, comparator_1_eq, comparator_2_eq, comparator_3_gt, decoder_1_out_0, decoder_1_out_1,
       decoder_1_out_2, decoder_1_out_3, decoder_2_out_1, decoder_2_out_2, decoder_2_out_3, decoder_2_out_4,
       decoder_2_out_5, decoder_2_out_6, decoder_2_out_7, decoder_2_out_8, indirect, nor_1_out, nor_2_out,
       or_1_out, or_2_out, or_4_out, run_nq, sub_1_c_o, sub_2_c_o;
  wire [0:0] lt_2_eq, lt_2_lt;
  wire [3:0] multiplexer_7_out;
  wire [15:0] add_1_s, add_2_s, multiplexer_2_out, multiplexer_3_out, register_1_q;
  wire [63:0] mul_mul, multiplexer_5_out, multiplexer_6_out, plus_s, sub_1_s, sub_2_s, write0_last_q;

  Comparator #(.Bits(16)) comparator_1 (.a(rw_addr), .b({16{1'b0}}), .eq(comparator_1_eq));  // open: gt, lt
  Break break_1 (.brk(write_en));
  RAMDualPort #(.AddrBits(16), .isProgramMemory("true"), .Bits(64), .generic("this.Label=args.ramLabel;")) ram (
    .A(rw_addr), .Din(write_val), .str(write_en), .C(C_t), .ld(1'b1), .D(out_val));
  Register #(.Bits(64)) write0_last (.D(write_val), .C(C_t), .en(comparator_1_eq), .Q(write0_last_q));
  // Probe on write0_last_q
  T_FF #(.Default(1)) run (.T(and_5_out), .C(C_t), .Q(running), .nQ(run_nq));
  nand nand_1 (C, running, clock);
  Counter #(.Bits(32)) counter_1 (.en(running), .C(C_t), .clr(1'b0), .out(cycle_cnt));  // open: ovf
  Multiplexer #(.Bits(16)) multiplexer_1 (.sel(C_t), .in_0(register_1_q), .in_1(add_2_s), .out(rw_addr));
  Break halt (.brk(run_nq));
  and and_1 (C_t, running, clock);
  Register #(.Bits(16)) register_1 (.D(multiplexer_2_out), .C(C), .en(1'b1), .Q(register_1_q));
  Break write (.brk(write_en));
  Add #(.Bits(16)) add_1 (.a(pc), .b({{14{1'b0}}, phase}), .c_i(1'b1), .s(add_1_s));  // open: c_o
  Add #(.Bits(16)) add_2 (.a({{14{1'b0}}, phase}), .b(pc), .c_i(1'b0), .s(add_2_s));  // open: c_o
  Multiplexer #(.Bits(16)) multiplexer_2 (
    .sel(indirect), .in_0(add_2_s), .in_1(out_val[15:0]), .out(multiplexer_2_out));
  Multiplexer #(.Bits(16)) multiplexer_3 (
    .sel(or_1_out), .in_0(add_1_s), .in_1(out_val[15:0]), .out(multiplexer_3_out));
  and and_2 (and_2_out, advance, or_2_out);
  Register #(.Bits(16)) register_2 (.D(multiplexer_3_out), .C(C_t), .en(and_2_out), .Q(pc));
  or or_1 (or_1_out, and_4_out, and_3_out);
  or or_2 (or_2_out, out_en, and_6_out, write_en);
  and and_3 (and_3_out, ~comparator_2_eq, decoder_2_out_5);  // And
  and and_4 (and_4_out, comparator_2_eq, decoder_2_out_6);
  Counter #(.Bits(2)) counter_2 (.en(advance), .C(C_t), .clr(and_2_out), .out(phase));  // open: ovf
  Register #(.Bits(64)) register_3 (.D(out_val), .C(C_t), .en(decoder_1_out_0), .Q(instr));
  Decoder #(.Selector_Bits(2)) decoder_1 (
    .sel(phase), .out_0(decoder_1_out_0), .out_1(decoder_1_out_1), .out_2(decoder_1_out_2),
    .out_3(decoder_1_out_3));
  Break jnz (.brk(decoder_2_out_5));
  Break jz (.brk(decoder_2_out_6));
  or or_3 (write_en, in_req, decoder_1_out_3);
  and and_5 (and_5_out, decoder_1_out_1, nor_2_out);
  Multiplexer #(.Bits(64)) multiplexer_4 (.sel(in_req), .in_0(r), .in_1(in_val), .out(write_val));
  Comparator #(.Signed("true"), .Bits(64)) comparator_2 (.a({64{1'b0}}), .b(X), .eq(comparator_2_eq));  // open: gt, lt
  Sub #(.Bits(64)) sub_1 (.a(instr), .b(64'h3e8), .c_i(1'b0), .s(sub_1_s), .c_o(sub_1_c_o));
  and and_6 (and_6_out, or_4_out, decoder_1_out_2);
  Multiplexer #(.Bits(64)) multiplexer_5 (.sel(sub_1_c_o), .in_0(sub_1_s), .in_1(instr), .out(multiplexer_5_out));
  and and_7 (and_7_out, ~sub_1_c_o, decoder_1_out_2);  // And
  or or_4 (or_4_out, decoder_2_out_5, decoder_2_out_6);
  and and_8 (and_8_out, in_req, ~in_avail);  // And
  Sub #(.Bits(64)) sub_2 (.a(multiplexer_5_out), .b(64'h64), .c_i(1'b0), .s(sub_2_s), .c_o(sub_2_c_o));
  not not_1 (advance, and_8_out);
  Break in (.brk(in_req));
  Multiplexer #(.Bits(64)) multiplexer_6 (
    .sel(sub_2_c_o), .in_0(sub_2_s), .in_1(multiplexer_5_out), .out(multiplexer_6_out));
  and and_9 (and_9_out, ~sub_2_c_o, decoder_1_out_1);  // And
  Comparator #(.Bits(64)) comparator_3 (.a(multiplexer_6_out), .b(64'h9), .gt(comparator_3_gt));  // open: eq, lt
  Break out (.brk(out_en));
  nor nor_1 (nor_1_out, and_7_out, and_9_out);
  and and_10 (indirect, nor_1_out, ~decoder_1_out_0);  // And
  Multiplexer #(.Bits(4)) multiplexer_7 (
    .sel(comparator_3_gt), .in_0(multiplexer_6_out[3:0]), .in_1(4'b1111), .out(multiplexer_7_out));
  and and_11 (in_req, decoder_2_out_3, decoder_1_out_1);
  and and_12 (out_en, decoder_2_out_4, decoder_1_out_1);
  Decoder #(.Selector_Bits(4)) decoder_2 (
    .sel(multiplexer_7_out), .out_1(decoder_2_out_1), .out_2(decoder_2_out_2), .out_3(decoder_2_out_3),
    .out_4(decoder_2_out_4), .out_5(decoder_2_out_5), .out_6(decoder_2_out_6), .out_7(decoder_2_out_7),
    .out_8(decoder_2_out_8));  // open: out_0, out_9, out_10, out_11, out_12, out_13, out_14, out_15
  Break lt (.brk(decoder_2_out_7));
  Register #(.Bits(64)) register_4 (.D(out_val), .C(C_t), .en(decoder_1_out_1), .Q(X));
  nor nor_2 (nor_2_out, decoder_2_out_1, decoder_2_out_2, decoder_2_out_3, decoder_2_out_4, decoder_2_out_5, decoder_2_out_6, decoder_2_out_7, decoder_2_out_8);
  Break eq (.brk(decoder_2_out_8));
  Add #(.Bits(64)) plus (.a(X), .b(Y), .c_i(1'b0), .s(plus_s));  // open: c_o
  Comparator #(.Signed("true"), .Bits(64)) lt_2 (.a(X), .b(Y), .eq(lt_2_eq[0]), .lt(lt_2_lt[0]));  // open: gt
  Mul #(.Signed("true"), .Bits(32)) mul (.a(X[31:0]), .b(Y[31:0]), .mul(mul_mul));
  Register #(.Bits(64)) register_5 (.D(out_val), .C(C_t), .en(decoder_1_out_2), .Q(Y));
  Multiplexer #(.Selector_Bits(4), .Bits(64)) multiplexer_8 (
    .sel(multiplexer_7_out), .in_0({64{1'b0}}), .in_1(plus_s), .in_2(mul_mul), .in_3({64{1'b0}}),
    .in_4({64{1'b0}}), .in_5({64{1'b0}}), .in_6({64{1'b0}}), .in_7({{63{1'b0}}, lt_2_lt[0]}),
    .in_8({{63{1'b0}}, lt_2_eq[0]}), .in_9({64{1'b0}}), .in_10({64{1'b0}}), .in_11({64{1'b0}}),
    .in_12({64{1'b0}}), .in_13({64{1'b0}}), .in_14({64{1'b0}}), .in_15({64{1'b0}}), .out(r));

  // Other names for the same wires on the sheet: ram_addr_1[15:0] = rw_addr; paramval[63:0] = out_val;
  //   ram_rval_1[63:0] = out_val; ram_we = write_en; ram_wval[63:0] = write_val

  // Notes on the sheet:
  //   clock: Hz: 100
  //   in_val: default 256
  //   in_avail: default 1
  //   param addr
  //   I-fetch (PC+phase)
  //   instr addr
  //   PC
  //   nextpc=
  //   pc+phase+1
  //   Instruction complete
  //   Conditional jumps
  //   phase
  //   Instruction decoding
  //   2-parameter instructions end on phase 2
  //   wait for input
  //   Bad instruction detection
  //   Parameter registers
  //   ALU
endmodule
